# Fritzing sketch portaschematic (saved by Fritzing 0.8.5b)
circuit board: 8.46667cm x 5.64444cm
breadboards: 1

parts:
  Componente1 = Arduino Mega 2560 (Rev3)
  Componente2 = Arduino Ethernet Shield (Rev3)
  R1 = Resistor [tolerance=±5% resistance=220 package=THT]
  R2 = Resistor [tolerance=±5% resistance=220 package=THT]
  R3 = Resistor [tolerance=±5% resistance=220 package=THT]
  LED1 = LED - 5mm [color="Red (633nm)" package="5 mm [THT]"]
  LED2 = LED - 5mm [color="Yellow (595nm)" package="5 mm [THT]"]
  LED3 = LED - 5mm [color="Green (555nm)" package="5 mm [THT]"]
  Componente3 = RFID-RC522-v2
  S2 = H-Bridge with L298N
  Alim_12v1 = 2.1mm Barrel Jack with Terminal Block
  M1 = DC Motor
  Componente4 = SRF05 Ultrasonic Rangefinder

nets:
  N1: Componente1.D34, S2.ENA
  N2: Componente1.D36, S2.IN1
  N3: Componente1.D38, S2.IN2
  N4: Componente1.D48, Componente3.RST
  N5: Componente1.D50, Componente3.MISO
  N6: Componente1.D51, Componente3.MOSI
  N7: Componente1.D52, Componente3.SCK
  N8: Componente1.D53, Componente3.SDA
  N9: Componente2.D8, Componente4.Trig
  N10: Componente2.PWM_D9, Componente4.Echo
  GND: Componente2.GND, LED1.anode, LED2.anode, LED3.anode, Componente3.GND, Componente4.GND
  N11: Componente2.PWM_D5, R2.Pin_1
  N12: Componente2.PWM_D6, R1.Pin_1
  N13: Componente2.D7, R3.Pin_1
  3V3: Componente2.3V3, Componente3.3.3V
  5V: Componente2.5V, Componente4.VCC
  N14: R1.Pin_0, LED2.cathode
  N15: R2.Pin_0, LED3.cathode
  N16: R3.Pin_0, LED1.cathode
  N17: S2.12V, Alim_12v1.POS
  N18: S2.GND, Alim_12v1.NEG
  N19: S2.M2-01, M1.pin_2
  N20: S2.M2-02, M1.pin_1

custom parts:
  RFID-RC522-v2: A simple China made RFID-RC522 Reader; do check the pin labels, as this is a MFRC522 based clone.
  H-Bridge with L298N: h-bridge
